// Logisim project Mikroprozessor_A_8_v0.1.circ as structural Verilog: 2 circuits, main circuit main
module main (
);

  wire adder_1_cout, Ain, ALo, and_1_out, and_2_out, Bin, Cin, CLK, clock_1_out, controlled_buffer_1_out,
       Cot, d_ff_1_qn, Fin, HLT, JMC, JMP, JMZ, ldJ, ldS, Mot, nor_1_out, Oin, Oot, or_1_out, RAi, Rin, Rot,
       seS, subtractor_1_bout;
  wire [3:0] register_7_q, register_7_q_2;
  wire [7:0] adder_1_out, bt_3_out_3, bt_5_out_3, ram_1_dout, register_1_q, register_2_q, register_3_q,
       register_4_q, register_5_q, register_6_q, register_8_q, register_9_q, rom_1_data, subtractor_1_out;
  wire [8:0] counter_1_q_2;
  wire [8:1] bt_1_out_3, counter_1_q;
  wire [19:19] rom_2_data;

  Counter #(.max('h1ff), .trigger("falling"), .width(9)) counter_1 (
    .load(or_1_out), .up(1'b1), .count(1'b1), .clk(CLK), .D({bt_1_out_3, 1'b0}),
    .Q({counter_1_q, counter_1_q_2[0]}));  // open: clr, carry
  Register #(.trigger("falling")) register_1 (.D(bt_5_out_3), .en(ldJ), .clk(CLK), .Q(register_1_q));  // open: clr
  Register #(.trigger("falling")) register_2 (.D(bt_5_out_3), .en(Ain), .clk(CLK), .Q(register_2_q));  // open: clr
  Register #(.trigger("falling")) register_3 (.D(bt_5_out_3), .en(Bin), .clk(CLK), .Q(register_3_q));  // open: clr
  BT bt_1 (.in_1(register_1_q), .in_2(or_1_out), .out_3(bt_1_out_3));
  assign controlled_buffer_1_out = register_5_q[0] ? adder_1_cout : 1'bz;  // Controlled_Buffer controlled_buffer_1
  assign controlled_buffer_1_out = register_5_q[1] ? subtractor_1_bout : 1'bz;  // Controlled_Buffer controlled_buffer_2
  Register register_4 (.D(counter_1_q), .en(ldS), .clk(CLK), .Q(register_4_q));  // open: clr
  or or_1 (or_1_out, and_2_out, JMP, and_1_out);
  and and_1 (and_1_out, controlled_buffer_1_out, JMC);
  Register register_5 (.D(bt_5_out_3), .en(Fin), .clk(CLK), .Q(register_5_q));  // open: clr
  Adder adder_1 (.a(register_2_q), .b(register_3_q), .out(adder_1_out), .cout(adder_1_cout));  // open: cin
  Subtractor subtractor_1 (
    .a(register_2_q), .b(register_3_q), .out(subtractor_1_out), .bout(subtractor_1_bout));  // open: bin
  BT bt_2 (.in_1(register_4_q), .in_2(seS), .out_3(bt_1_out_3));
  BT bt_3 (.in_1(adder_1_out), .in_2(register_5_q[0]), .out_3(bt_3_out_3));
  BT bt_4 (.in_1(subtractor_1_out), .in_2(register_5_q[1]), .out_3(bt_3_out_3));
  and and_2 (and_2_out, JMZ, nor_1_out);
  nor nor_1 (nor_1_out, register_6_q[7], register_6_q[6], register_6_q[5], register_6_q[4], register_6_q[3], register_6_q[2], register_6_q[1], register_6_q[0]);
  Register register_6 (.D(bt_3_out_3), .en(1'b1), .clk(CLK), .Q(register_6_q));  // open: clr
  ROM #(.dataWidth(16)) rom_1 (.addr(counter_1_q), .data({counter_1_q_2[8:1], rom_1_data}));
  BT bt_5 (.in_1(register_6_q), .in_2(ALo), .out_3(bt_5_out_3));
  Hex_Digit_Display hex_digit_display_1 (.value(register_7_q_2));  // open: dp
  Register #(.trigger("falling")) register_7 (
    .D(bt_5_out_3), .en(Oin), .clk(CLK), .Q({register_7_q_2, register_7_q}));  // open: clr
  Hex_Digit_Display hex_digit_display_2 (.value(register_7_q));  // open: dp
  BT bt_6 (.in_1({register_7_q_2, register_7_q}), .in_2(Oot), .out_3(bt_5_out_3));
  // Probe on {counter_1_q_2[8:1], rom_1_data}
  // Probe on bt_5_out_3
  Register register_8 (.D(bt_5_out_3), .en(RAi), .clk(CLK), .Q(register_8_q));  // open: clr
  RAM ram_1 (.addr(register_8_q), .we(Rin), .oe(1'b1), .clk(CLK), .din(bt_5_out_3), .dout(ram_1_dout));
  BT bt_7 (.in_1(rom_1_data), .in_2(Mot), .out_3(bt_5_out_3));
  Clock clock_1 (.out(clock_1_out));
  Register #(.trigger("high")) register_9 (.D(bt_5_out_3), .en(Cin), .clk(CLK), .Q(register_9_q));  // open: clr
  and and_3 (CLK, clock_1_out, d_ff_1_qn);
  D_Flip_Flop d_ff_1 (.Qn(d_ff_1_qn), .preset(HLT));  // open: D, clk, Q, reset
  ROM #(.addrWidth(9), .dataWidth(20)) rom_2 (
    .addr(counter_1_q_2),
    .data({rom_2_data[19], Oot, Oin, JMZ, JMC, JMP, ldJ, seS, ldS, ALo, Fin, Rot, Rin, RAi, Mot, Cot, Cin, Bin, Ain, HLT}));
  BT bt_8 (.in_1(register_9_q), .in_2(Cot), .out_3(bt_5_out_3));
  BT bt_9 (.in_1(ram_1_dout), .in_2(Rot), .out_3(bt_5_out_3));

  // Notes on the sheet:
  //   contents of rom_1 (hex, n*v repeats v):
  //   401 300 600 414 302 407 303 0 101 501 702 900 c01 0 101 500 900 c00 703 a00 400 300 301 302 303 700
  //   a00
  //   contents of rom_2 (hex, n*v repeats v):
  //   60 102 60 104 60 108 60 90 28 0 60 480 60 300 60 2100 10000 0 8000 0 4000 0 1 0 60 20100 60 40080
endmodule

module BT (
  input  [7:0] in_1,
  input  in_2,
  output [7:0] out_3
);

  assign out_3 = in_2 ? in_1 : 8'bz;  // Controlled_Buffer controlled_buffer_1
endmodule
